# Fritzing sketch wiring (saved by Fritzing 0.9.4)
breadboards: 1

parts:
  Part1 = Arduino Uno (Rev3)
  J1 = Power Jack [package=power_jack_slot]
  LCD2 = LCD screen
  LCM1602_IIC1 = LCM1602 IIC [part_number="LCM1602 IIC" chip_label="LCM1602 IIC" package="DIP (Dual Inline) [THT]"]
  U1 = SWITCH-SPST-2 [package=switch-spst-vertical]
  S1 = Pushbutton [package="[THT]"]
  Part2 = Coin Acceptor - 6-Coin version
  LM1 = RioRand LM2596

nets:
  N1: Part1.A4/SDA, LCM1602_IIC1.SDA
  N2: Part1.A5/SCL, LCM1602_IIC1.SCL
  N3: Part1.D8, S1.Pin_3
  N4: Part1.D2, Part2.SIG
  5V: Part1.5V, LCM1602_IIC1.VCC, LM1.Pin_3
  GND: Part1.GND, LCM1602_IIC1.GND, S1.Pin_1, LM1.Pin_4
  GND_2: J1.GNDBREAK, J1.GND, Part2.GND, LM1.Pin_2
  N5: J1.PWR, U1.P
  VSS: LCD2.VSS, LCM1602_IIC1.VSS
  VDD: LCD2.VDD, LCM1602_IIC1.VDD
  N6: LCD2.V0, LCM1602_IIC1.V0
  N7: LCD2.RS, LCM1602_IIC1.RS
  N8: LCD2.R/W, LCM1602_IIC1.RW
  N9: LCD2.E, LCM1602_IIC1.E
  N10: LCD2.DB0, LCM1602_IIC1.D0
  N11: LCD2.DB1, LCM1602_IIC1.D1
  N12: LCD2.DB2, LCM1602_IIC1.D2
  N13: LCD2.DB3, LCM1602_IIC1.D3
  N14: LCD2.DB4, LCM1602_IIC1.D4
  N15: LCD2.DB5, LCM1602_IIC1.D5
  N16: LCD2.DB6, LCM1602_IIC1.D6
  N17: LCD2.DB7, LCM1602_IIC1.D7
  N18: LCD2.LED+, LCM1602_IIC1.A
  N19: LCD2.LED-, LCM1602_IIC1.K
  N20: LCM1602_IIC1.LED_A, LCM1602_IIC1.LED_B
  N21: U1.O, Part2.12V, LM1.Pin_1

custom parts:
  LCM1602 IIC: I2C-Module to use a 1602 or 2004 LCD on with the wire.h libory Serial LCD Modul
  Coin Acceptor - 6-Coin version: 12V coin acceptor that can handle up to 6 different denominations. Output is either pulse width, serial, or single pin per coin value.
